// Logisim project 2-2-1.circ as structural Verilog
module main (
  input  a,
  input  b,
  input  cin,
  output s,
  output cout
);

  wire and_1_out, and_2_out, xor_1_out;

  xor xor_1 (xor_1_out, a, b);
  xor xor_2 (s, xor_1_out, cin);
  and and_1 (and_1_out, cin, xor_1_out);
  and and_2 (and_2_out, b, a);
  or or_1 (cout, and_1_out, and_2_out);
endmodule
