// Logisim project 2-2-2.circ as structural Verilog: 1 circuit, main circuit main
module main (
  input  B3,
  input  A,
  input  B2,
  input  A2,
  input  B1,
  input  A1,
  input  B0,
  input  A0,
  input  CIN,
  output C3,
  output C1,
  output C2,
  output C,
  output COUT
);

  wire adder_1_cout, adder_2_cout, adder_3_cout, adder_4_cout, xor_1_out, xor_3_out, xor_4_out, xor_5_out;

  xor xor_1 (xor_1_out, A, CIN);
  Adder #(.width(1)) adder_1 (.a(xor_1_out), .b(B3), .out(C3), .cin(adder_2_cout), .cout(adder_1_cout));
  xor xor_2 (COUT, adder_1_cout, adder_2_cout);
  xor xor_3 (xor_3_out, A2, CIN);
  Adder #(.width(1)) adder_2 (.a(xor_3_out), .b(B2), .out(C2), .cin(adder_3_cout), .cout(adder_2_cout));
  xor xor_4 (xor_4_out, A1, CIN);
  Adder #(.width(1)) adder_3 (.a(xor_4_out), .b(B1), .out(C1), .cin(adder_4_cout), .cout(adder_3_cout));
  xor xor_5 (xor_5_out, A0, CIN);
  Adder #(.width(1)) adder_4 (.a(xor_5_out), .b(B0), .out(C), .cin(CIN), .cout(adder_4_cout));
endmodule
